# Fritzing sketch Untitled Sketch 2 (saved by Fritzing 0.9.3b)
breadboards: 1

parts:
  WeMos_D1_Mini1 = WeMos D1 Mini
  S1 = Round Pushbutton
  Bauteil1 = IR Receiver Breakout [package=PCB]
  Bauteil2 = IR Receiver Breakout [package=PCB]
  Grove1 = Grove 4 Digit Display
  Grove2 = Grove 4 Digit Display
  Conductivity_Circuit1 = Conductivity Circuit  # not connected

nets:
  VCC: WeMos_D1_Mini1.5V, Bauteil1.VCC, Bauteil2.VCC, Grove1.VCC, Grove2.VCC
  N1: WeMos_D1_Mini1.D2, S1.leg0
  N2: WeMos_D1_Mini1.D4, Bauteil1.GND
  N3: WeMos_D1_Mini1.D5, Bauteil2.GND
  N4: WeMos_D1_Mini1.D6, Grove2.DIO
  N5: WeMos_D1_Mini1.D7, Grove1.DIO
  GND: WeMos_D1_Mini1.G, S1.leg1, Bauteil1.OUT, Bauteil2.OUT, Grove1.GND, Grove2.GND
